# Fritzing sketch ldr_servo (saved by Fritzing 0.9.3b)
breadboards: 1

parts:
  R1 = Photocell (LDR) [package=THT]
  R2 = Photocell (LDR) [package=THT]
  Part1 = Arduino Uno (Rev3)
  LED1 = smd LED [color="Red (633nm)" package="1206 [SMD]"]
  R3 = Resistor [tolerance=±5% resistance=220 package="0402 [SMD]"]

nets:
  N1: R1.pin_0, R2.pin_1, Part1.GND, LED1.cathode
  N2: R1.pin_1, Part1.A0
  N3: R2.pin_0, Part1.A2
  N4: LED1.anode, R3.Pin_0
