# Fritzing sketch led_blink (saved by Fritzing 0.9.3b)
breadboards: 1

parts:
  Part1 = Arduino Uno (Rev3)  # not connected
  R1 = Resistor [tolerance=±5% resistance=220 package="0805 [SMD]"]
  LED1 = smd LED [color="Red (635nm)" package="1206 [SMD]"]

nets:
  N1: R1.Pin_1, LED1.anode
